// Logisim project mubin2107090notunta.circ as structural Verilog
module circuitimp (
  input  Clock_Pulse,
  output clk_out,
  output rc,
  output rb,
  output ra,
  output r0,
  output lb,
  output la,
  output l0
);

  wire and_2_out, and_3_out, and_4_out, and_5_out, and_6_out, and_7_out, j_k_ff_1_qn, j_k_ff_2_qn,
       j_k_ff_3_qn, j_k_ff_4_qn, j_k_ff_5_qn, j_k_ff_6_qn, j_k_ff_7_qn, nand_1_out, not_1_out, not_2_out;

  and and_1 (clk_out, j_k_ff_1_qn, j_k_ff_2_qn, j_k_ff_3_qn);
  J_K_Flip_Flop j_k_ff_1 (.J(1'b1), .clk(nand_1_out), .K(1'b1), .Q(l0), .Qn(j_k_ff_1_qn));  // open: preset, en, reset
  and and_2 (and_2_out, l0, j_k_ff_3_qn);
  J_K_Flip_Flop j_k_ff_2 (
    .J(and_2_out), .clk(nand_1_out), .K(l0), .Q(la), .Qn(j_k_ff_2_qn));  // open: preset, en, reset
  and and_3 (and_3_out, l0, la);
  J_K_Flip_Flop j_k_ff_3 (
    .J(and_3_out), .clk(nand_1_out), .K(l0), .Q(lb), .Qn(j_k_ff_3_qn));  // open: preset, en, reset
  nand nand_1 (nand_1_out, rc, not_1_out, not_2_out, r0);
  and and_4 (and_4_out, l0, la, j_k_ff_3_qn, j_k_ff_7_qn, j_k_ff_6_qn, j_k_ff_5_qn, j_k_ff_4_qn);
  not not_1 (not_1_out, rb);
  not not_2 (not_2_out, ra);
  J_K_Flip_Flop j_k_ff_4 (
    .J(1'b1), .clk(Clock_Pulse), .K(1'b1), .Q(r0), .Qn(j_k_ff_4_qn), .preset(and_4_out));  // open: en, reset
  and and_5 (and_5_out, r0, j_k_ff_7_qn);
  J_K_Flip_Flop j_k_ff_5 (
    .J(and_5_out), .clk(Clock_Pulse), .K(r0), .Q(ra), .Qn(j_k_ff_5_qn), .reset(and_4_out));  // open: preset, en
  and and_6 (and_6_out, ra, r0);
  J_K_Flip_Flop j_k_ff_6 (
    .J(and_6_out), .clk(Clock_Pulse), .K(and_6_out), .Q(rb), .Qn(j_k_ff_6_qn), .reset(and_4_out));  // open: preset, en
  and and_7 (and_7_out, rb, and_6_out);
  J_K_Flip_Flop j_k_ff_7 (
    .J(and_7_out), .clk(Clock_Pulse), .K(r0), .Q(rc), .Qn(j_k_ff_7_qn), .reset(and_4_out));  // open: preset, en

  // Notes on the sheet:
  //   2107090
endmodule
